// Logisim project CombinationalLogic.circ as structural Verilog: 8 circuits, main circuit main
module main (
  input  in_1,
  input  in_2,
  input  in_3,
  input  in_4,
  input  in_5,
  input  in_6,
  input  [2:0] in_7,
  input  [2:0] in_8,
  input  [1:0] in_9,
  input  [2:0] in_10,
  input  [2:0] in_11,
  input  in_12,
  input  in_13,
  input  in_14,
  input  [3:0] in_15,
  input  [3:0] in_16,
  input  \_4_2编码器 ,
  input  in_18,
  input  in_19,
  input  in_20,
  input  \_4_2优先编码器 ,
  input  in_22,
  input  in_23,
  input  in_24,
  input  \_4_2优先编码器2 ,
  input  in_26,
  input  in_27,
  input  in_28,
  input  \_4_2优先编码器3 ,
  input  in_30,
  input  in_31,
  input  in_32,
  output out_33,
  output out_34,
  output out_35,
  output out_36,
  output out_37,
  output out_38,
  output out_39,
  output out_40,
  output [2:0] out_41,
  output out_42,
  output out_43,
  output out_44,
  output out_45,
  output out_46,
  output l,
  output h,
  output out_49,
  output out_50,
  output out_51,
  output out_52
);

  wire and_2_out, and_3_out, and_4_out, and_5_out, and_6_out, and_7_out, and_8_out, and_9_out, and_10_out,
       and_11_out, and_12_out, and_13_out, and_14_out, and_23_out, and_24_out, and_31_out,
       decoder2_4_1_out_3, decoder2_4_1_out_4, decoder2_4_1_out_5, decoder2_4_1_out_6, decoder2_4_2_out_3,
       decoder2_4_2_out_4, decoder2_4_2_out_5, decoder2_4_2_out_6, decoder2_4_3_out_3, decoder2_4_3_out_4,
       decoder2_4_3_out_5, decoder2_4_3_out_6, decoder2_4_4_out_3, decoder2_4_4_out_4, decoder2_4_4_out_5,
       decoder2_4_4_out_6, decoder_1_out0, decoder_1_out1, decoder_1_out2, decoder_1_out3, decoder_1_out4,
       decoder_1_out5, decoder_1_out6, decoder_1_out7, decoder_1_out8, decoder_1_out9, decoder_1_out10,
       decoder_1_out11, decoder_1_out12, decoder_1_out13, decoder_1_out14, decoder_1_out15, decoder_2_out0,
       decoder_2_out1, decoder_2_out2, decoder_2_out3, decoder_3_out0, decoder_3_out1, decoder_3_out2,
       decoder_3_out3, decoder_3_out4, decoder_3_out5, decoder_3_out6, decoder_3_out7, decoder_3_out8,
       decoder_3_out9, decoder_3_out10, decoder_3_out11, decoder_3_out12, decoder_3_out13, decoder_3_out14,
       decoder_3_out15, dipswitch_1_p1, dipswitch_1_p2, dipswitch_1_p3, dipswitch_1_p4, dipswitch_1_p5,
       dipswitch_1_p6, dipswitch_1_p7, dipswitch_1_p8, dipswitch_1_p9, dipswitch_1_p10, dipswitch_1_p11,
       dipswitch_1_p12, dipswitch_1_p13, dipswitch_1_p14, dipswitch_1_p15, dipswitch_1_p16, dipswitch_2_p1,
       dipswitch_3_p1, dipswitch_3_p2, dipswitch_3_p3, dipswitch_4_p1, dipswitch_4_p2, dipswitch_4_p3,
       dipswitch_4_p4, dipswitch_4_p5, dipswitch_5_p1, dipswitch_5_p2, dipswitch_5_p3, dipswitch_5_p4,
       dipswitch_6_p1, dipswitch_6_p2, dipswitch_6_p3, dipswitch_6_p4, full_adder_1_cout, full_adder_2_cout,
       full_adder_3_cout, half_adder_1_c, half_adder_1_s, half_adder_2_c, half_adder_3_c, not_1_out,
       not_2_out, not_3_out, not_4_out, not_5_out, not_6_out, not_7_out, not_8_out, not_9_out, not_10_out,
       not_11_out, not_12_out, not_13_out, not_14_out, not_15_out, not_16_out, or_1_out, or_6_out, or_7_out,
       or_8_out, or_9_out, or_10_out, or_11_out, or_12_out, or_21_out, or_22_out, or_23_out, or_24_out,
       or_25_out, or_26_out, or_27_out, seven_segment_circuit10_1_out_2, seven_segment_circuit10_1_out_3,
       seven_segment_circuit10_1_out_4, seven_segment_circuit10_1_out_5, seven_segment_circuit10_1_out_6,
       seven_segment_circuit10_1_out_7, seven_segment_circuit10_1_out_8, seven_segment_circuit10_1_out_9,
       seven_segment_circuit16_1_a, seven_segment_circuit16_1_b, seven_segment_circuit16_1_c,
       seven_segment_circuit16_1_d, seven_segment_circuit16_1_e, seven_segment_circuit16_1_f,
       seven_segment_circuit16_1_g, seven_segment_circuit16_2_a, seven_segment_circuit16_2_b,
       seven_segment_circuit16_2_c, seven_segment_circuit16_2_d, seven_segment_circuit16_2_e,
       seven_segment_circuit16_2_f, seven_segment_circuit16_2_g, seven_segment_circuit16_3_a,
       seven_segment_circuit16_3_b, seven_segment_circuit16_3_c, seven_segment_circuit16_3_d,
       seven_segment_circuit16_3_e, seven_segment_circuit16_3_f, seven_segment_circuit16_3_g, xnor_1_out,
       xnor_2_out, xnor_3_out, xnor_4_out;
  wire [2:0] and_25_out, and_26_out, and_27_out, and_28_out, bit_extender_1_out, bit_extender_2_out,
       bit_extender_3_out, bit_extender_4_out;
  wire [3:0] and_29_out, and_30_out, bit_extender_5_out, bit_extender_6_out, half_adder_2_s, low1_out,
       undriven;

  // DipSwitch #(.number(16)) dipswitch_1: pin names not known; wires that end beside it: dipswitch_1_p1, dipswitch_1_p2, dipswitch_1_p3, dipswitch_1_p4, dipswitch_1_p5, dipswitch_1_p6, dipswitch_1_p7, dipswitch_1_p8, dipswitch_1_p9, dipswitch_1_p10, dipswitch_1_p11, dipswitch_1_p12, dipswitch_1_p13, dipswitch_1_p14, dipswitch_1_p15, dipswitch_1_p16
  not not_1 (not_1_out, in_1);
  not not_2 (not_2_out, in_4);
  not not_3 (not_3_out, in_6);
  Decoder #(.enable("false"), .select(4)) decoder_1 (
    .out0(decoder_1_out0), .out1(decoder_1_out1), .out2(decoder_1_out2), .out3(decoder_1_out3),
    .out4(decoder_1_out4), .out5(decoder_1_out5), .out6(decoder_1_out6), .out7(decoder_1_out7),
    .out8(decoder_1_out8), .out9(decoder_1_out9), .out10(decoder_1_out10), .out11(decoder_1_out11),
    .out12(decoder_1_out12), .out13(decoder_1_out13), .out14(decoder_1_out14), .out15(decoder_1_out15),
    .sel(in_15));
  or low1 (low1_out[0], dipswitch_1_p2, dipswitch_1_p4, dipswitch_1_p6, dipswitch_1_p8, dipswitch_1_p10, dipswitch_1_p12, dipswitch_1_p14, dipswitch_1_p16);
  or or_1 (or_1_out, decoder_1_out15, decoder_1_out14, decoder_1_out13, decoder_1_out12, decoder_1_out11, decoder_1_out10);
  or or_2 (low1_out[1], dipswitch_1_p3, dipswitch_1_p4, dipswitch_1_p7, dipswitch_1_p8, dipswitch_1_p11, dipswitch_1_p12, dipswitch_1_p15, dipswitch_1_p16);
  or or_3 (low1_out[2], dipswitch_1_p5, dipswitch_1_p6, dipswitch_1_p7, dipswitch_1_p8, dipswitch_1_p13, dipswitch_1_p14, dipswitch_1_p15, dipswitch_1_p16);
  or high1 (low1_out[3], dipswitch_1_p9, dipswitch_1_p10, dipswitch_1_p11, dipswitch_1_p12, dipswitch_1_p13, dipswitch_1_p14, dipswitch_1_p15, dipswitch_1_p16);
  or or_4 (out_45, in_18, in_20);
  or or_5 (out_46, in_19, in_20);
  decoder2_4 decoder2_4_1 (
    .in_1(in_1), .in_2(not_2_out), .out_3(decoder2_4_1_out_3), .out_4(decoder2_4_1_out_4),
    .out_5(decoder2_4_1_out_5), .out_6(decoder2_4_1_out_6));
  decoder2_4 decoder2_4_2 (
    .in_1(not_1_out), .in_2(in_4), .out_3(decoder2_4_2_out_3), .out_4(decoder2_4_2_out_4),
    .out_5(decoder2_4_2_out_5), .out_6(decoder2_4_2_out_6));
  decoder2_4 decoder2_4_3 (
    .in_1(in_4), .in_2(in_6), .out_3(decoder2_4_3_out_3), .out_4(decoder2_4_3_out_4),
    .out_5(decoder2_4_3_out_5), .out_6(decoder2_4_3_out_6));
  decoder2_4 decoder2_4_4 (
    .in_1(not_2_out), .in_2(not_3_out), .out_3(decoder2_4_4_out_3), .out_4(decoder2_4_4_out_4),
    .out_5(decoder2_4_4_out_5), .out_6(decoder2_4_4_out_6));
  _7_Segment_Display u_7_segment_display_1 (
    .g(seven_segment_circuit16_1_g), .f(seven_segment_circuit16_1_f), .a(seven_segment_circuit16_1_a),
    .b(seven_segment_circuit16_1_b), .e(seven_segment_circuit16_1_e), .d(seven_segment_circuit16_1_d),
    .c(seven_segment_circuit16_1_c));  // open: dp
  not not_4 (not_4_out, in_22);
  // AND_Gate and_1 has open pins: in0=\_4_2优先编码器 , in1=not_4_out, in2=not_5_out, in3=not_6_out, out=open
  not not_5 (not_5_out, in_23);
  not not_6 (not_6_out, in_24);
  not not_7 (not_7_out, in_23);
  and and_2 (and_2_out, in_22, not_7_out, not_8_out);
  not not_8 (not_8_out, in_24);
  and and_3 (and_3_out, in_23, not_9_out);
  not not_9 (not_9_out, in_24);
  not not_10 (not_10_out, in_27);
  and and_4 (and_4_out, in_26, not_10_out, not_11_out);
  not not_11 (not_11_out, in_28);
  and and_5 (and_5_out, in_27, not_12_out);
  not not_12 (not_12_out, in_28);
  not not_13 (not_13_out, in_31);
  and and_6 (and_6_out, in_30, not_13_out, not_14_out);
  not not_14 (not_14_out, in_32);
  and and_7 (and_7_out, decoder2_4_1_out_3, decoder2_4_2_out_6);
  and and_8 (and_8_out, decoder2_4_1_out_4, decoder2_4_2_out_5);
  and and_9 (and_9_out, decoder2_4_1_out_6, decoder2_4_2_out_3);
  and and_10 (and_10_out, decoder2_4_1_out_5, decoder2_4_2_out_4);
  and and_11 (and_11_out, decoder2_4_3_out_4, decoder2_4_4_out_5);
  and and_12 (and_12_out, decoder2_4_3_out_3, decoder2_4_4_out_6);
  and and_13 (and_13_out, decoder2_4_3_out_5, decoder2_4_4_out_4);
  and and_14 (and_14_out, decoder2_4_3_out_6, decoder2_4_4_out_3);
  seven_segment_circuit16 seven_segment_circuit16_1 (
    .in_1(low1_out), .a(seven_segment_circuit16_1_a), .b(seven_segment_circuit16_1_b),
    .c(seven_segment_circuit16_1_c), .d(seven_segment_circuit16_1_d), .e(seven_segment_circuit16_1_e),
    .f(seven_segment_circuit16_1_f), .g(seven_segment_circuit16_1_g));
  or or_6 (or_6_out, decoder_1_out0, decoder_1_out2, decoder_1_out3, decoder_1_out9, decoder_1_out5, decoder_1_out6, decoder_1_out7, decoder_1_out8);
  or or_7 (or_7_out, decoder_1_out0, decoder_1_out1, decoder_1_out2, decoder_1_out3, decoder_1_out4, decoder_1_out8, decoder_1_out7, decoder_1_out9);
  or or_8 (or_8_out, decoder_1_out0, decoder_1_out1, decoder_1_out3, decoder_1_out4, decoder_1_out5, decoder_1_out6, decoder_1_out7, decoder_1_out8, decoder_1_out9);
  or or_9 (or_9_out, decoder_1_out0, decoder_1_out2, decoder_1_out3, decoder_1_out5, decoder_1_out6, decoder_1_out8, decoder_1_out9);
  or or_10 (or_10_out, decoder_1_out0, decoder_1_out2, decoder_1_out6, decoder_1_out8);
  or or_11 (or_11_out, decoder_1_out0, decoder_1_out4, decoder_1_out5, decoder_1_out6, decoder_1_out8, decoder_1_out9);
  or or_12 (or_12_out, decoder_1_out2, decoder_1_out3, decoder_1_out4, decoder_1_out5, decoder_1_out6, decoder_1_out8, decoder_1_out9);
  or or_13 (l, in_24, and_2_out);
  or or_14 (h, and_3_out, in_24);
  or or_15 (out_49, in_28, and_4_out);
  or or_16 (out_50, and_5_out, in_28);
  or or_17 (out_51, and_6_out, in_32);
  or or_18 (out_52, in_31, in_32);
  and and_15 (out_33, and_8_out, and_12_out);
  and and_16 (out_34, and_8_out, and_11_out);
  and and_17 (out_36, and_7_out, and_13_out);
  and and_18 (out_37, and_7_out, and_14_out);
  and and_19 (out_38, and_12_out, and_9_out);
  and and_20 (out_39, and_9_out, and_11_out);
  buf and_21 (out_40, and_13_out);  // AND_Gate
  and and_22 (out_42, and_10_out, and_14_out);
  _7_Segment_Display u_7_segment_display_2 (
    .g(or_12_out), .f(or_11_out), .a(or_6_out), .b(or_7_out), .e(or_10_out), .d(or_9_out), .c(or_8_out),
    .dp(or_1_out));
  Decoder #(.enable("false"), .select(2)) decoder_2 (
    .out0(decoder_2_out0), .out1(decoder_2_out1), .out2(decoder_2_out2), .out3(decoder_2_out3), .sel(in_9));
  not not_15 (not_15_out, in_3);
  assign bit_extender_1_out = {{2{decoder_2_out0}}, decoder_2_out0};  // Bit_Extender bit_extender_1
  and and_23 (and_23_out, in_2, not_15_out);
  and and_24 (and_24_out, in_3, in_5);
  assign bit_extender_2_out = {{2{decoder_2_out3}}, decoder_2_out3};  // Bit_Extender bit_extender_2
  assign bit_extender_3_out = {{2{decoder_2_out1}}, decoder_2_out1};  // Bit_Extender bit_extender_3
  assign bit_extender_4_out = {{2{decoder_2_out2}}, decoder_2_out2};  // Bit_Extender bit_extender_4
  or or_19 (out_35, and_23_out, and_24_out);
  assign and_25_out = in_7 & bit_extender_1_out;  // AND_Gate and_25, 3 bits wide
  assign and_26_out = in_8 & bit_extender_3_out;  // AND_Gate and_26, 3 bits wide
  assign and_27_out = bit_extender_4_out & in_10;  // AND_Gate and_27, 3 bits wide
  assign and_28_out = bit_extender_2_out & in_11;  // AND_Gate and_28, 3 bits wide
  Decoder #(.enable("false"), .select(4)) decoder_3 (
    .out0(decoder_3_out0), .out1(decoder_3_out1), .out2(decoder_3_out2), .out3(decoder_3_out3),
    .out4(decoder_3_out4), .out5(decoder_3_out5), .out6(decoder_3_out6), .out7(decoder_3_out7),
    .out8(decoder_3_out8), .out9(decoder_3_out9), .out10(decoder_3_out10), .out11(decoder_3_out11),
    .out12(decoder_3_out12), .out13(decoder_3_out13), .out14(decoder_3_out14), .out15(decoder_3_out15),
    .sel(in_16));
  assign out_41 = and_25_out | and_26_out | and_27_out | and_28_out;  // OR_Gate or_20, 3 bits wide
  // DipSwitch #(.number(5)) dipswitch_2: pin names not known; wires that end beside it: dipswitch_2_p1
  assign bit_extender_5_out = {{3{not_16_out}}, not_16_out};  // Bit_Extender bit_extender_5
  not not_16 (not_16_out, dipswitch_2_p1);
  assign bit_extender_6_out = {{3{dipswitch_2_p1}}, dipswitch_2_p1};  // Bit_Extender bit_extender_6
  assign and_29_out = undriven & bit_extender_5_out;  // AND_Gate and_29, 4 bits wide
  assign and_30_out = undriven & bit_extender_6_out;  // AND_Gate and_30, 4 bits wide
  or or_21 (or_21_out, decoder_3_out10, decoder_3_out12, decoder_3_out0, decoder_3_out2, decoder_3_out3, decoder_3_out9, decoder_3_out5, decoder_3_out6, decoder_3_out7, decoder_3_out8, decoder_3_out14, decoder_3_out15);
  or or_22 (or_22_out, decoder_3_out10, decoder_3_out0, decoder_3_out1, decoder_3_out2, decoder_3_out3, decoder_3_out4, decoder_3_out8, decoder_3_out7, decoder_3_out9, decoder_3_out13);
  or or_23 (or_23_out, decoder_3_out5, decoder_3_out10, decoder_3_out0, decoder_3_out1, decoder_3_out3, decoder_3_out4, decoder_3_out6, decoder_3_out7, decoder_3_out8, decoder_3_out9, decoder_3_out11, decoder_3_out13);
  or or_24 (or_24_out, decoder_3_out11, decoder_3_out12, decoder_3_out0, decoder_3_out2, decoder_3_out3, decoder_3_out5, decoder_3_out6, decoder_3_out8, decoder_3_out9, decoder_3_out13, decoder_3_out14);
  seven_segment_circuit10 seven_segment_circuit10_1 (
    .in_1(and_29_out), .out_2(seven_segment_circuit10_1_out_2), .out_3(seven_segment_circuit10_1_out_3),
    .out_4(seven_segment_circuit10_1_out_4), .out_5(seven_segment_circuit10_1_out_5),
    .out_6(seven_segment_circuit10_1_out_6), .out_7(seven_segment_circuit10_1_out_7),
    .out_8(seven_segment_circuit10_1_out_8), .out_9(seven_segment_circuit10_1_out_9));
  seven_segment_circuit16 seven_segment_circuit16_2 (
    .in_1(and_30_out), .a(seven_segment_circuit16_2_a), .b(seven_segment_circuit16_2_b),
    .c(seven_segment_circuit16_2_c), .d(seven_segment_circuit16_2_d), .e(seven_segment_circuit16_2_e),
    .f(seven_segment_circuit16_2_f), .g(seven_segment_circuit16_2_g));
  or or_25 (or_25_out, decoder_3_out10, decoder_3_out11, decoder_3_out12, decoder_3_out0, decoder_3_out2, decoder_3_out6, decoder_3_out8, decoder_3_out13, decoder_3_out14, decoder_3_out15);
  _7_Segment_Display u_7_segment_display_3 (
    .g(seven_segment_circuit16_2_g), .f(seven_segment_circuit16_2_f), .a(seven_segment_circuit16_2_a),
    .b(seven_segment_circuit16_2_b), .e(seven_segment_circuit16_2_e), .d(seven_segment_circuit16_2_d),
    .c(seven_segment_circuit16_2_c));  // open: dp
  or or_26 (or_26_out, decoder_3_out10, decoder_3_out11, decoder_3_out0, decoder_3_out4, decoder_3_out5, decoder_3_out12, decoder_3_out6, decoder_3_out8, decoder_3_out9, decoder_3_out14, decoder_3_out15);
  or or_27 (or_27_out, decoder_3_out5, decoder_3_out10, decoder_3_out11, decoder_3_out2, decoder_3_out3, decoder_3_out4, decoder_3_out6, decoder_3_out8, decoder_3_out9, decoder_3_out13, decoder_3_out14, decoder_3_out15);
  _7_Segment_Display u_7_segment_display_4 (
    .g(seven_segment_circuit10_1_out_8), .f(seven_segment_circuit10_1_out_7),
    .a(seven_segment_circuit10_1_out_2), .b(seven_segment_circuit10_1_out_3),
    .e(seven_segment_circuit10_1_out_6), .d(seven_segment_circuit10_1_out_5),
    .c(seven_segment_circuit10_1_out_4), .dp(seven_segment_circuit10_1_out_9));
  _7_Segment_Display u_7_segment_display_5 (
    .g(or_27_out), .f(or_26_out), .a(or_21_out), .b(or_22_out), .e(or_25_out), .d(or_24_out), .c(or_23_out));  // open: dp
  // DipSwitch #(.number(4)) dipswitch_3: pin names not known; wires that end beside it: dipswitch_3_p1, dipswitch_3_p2, dipswitch_3_p3
  // DipSwitch #(.number(4)) dipswitch_4: pin names not known; wires that end beside it: dipswitch_4_p1, dipswitch_4_p2, dipswitch_4_p3, dipswitch_4_p4, dipswitch_4_p5
  // DipSwitch #(.number(4)) dipswitch_5: pin names not known; wires that end beside it: dipswitch_5_p1, dipswitch_5_p2, dipswitch_5_p3, dipswitch_5_p4
  // DipSwitch #(.number(4)) dipswitch_6: pin names not known; wires that end beside it: dipswitch_6_p1, dipswitch_6_p2, dipswitch_6_p3, dipswitch_6_p4
  xnor xnor_1 (xnor_1_out, dipswitch_3_p1, dipswitch_4_p2);
  xnor xnor_2 (xnor_2_out, dipswitch_3_p2, dipswitch_4_p3);
  xnor xnor_3 (xnor_3_out, dipswitch_3_p3, dipswitch_4_p4);
  xnor xnor_4 (xnor_4_out, dipswitch_4_p1, dipswitch_4_p5);
  and and_31 (and_31_out, xnor_1_out, xnor_2_out, xnor_3_out, xnor_4_out);
  LED led_1 (.in(and_31_out));
  Half_adder half_adder_1 (.in_1(in_12), .in_2(in_13), .S(half_adder_1_s), .C(half_adder_1_c));
  Half_adder half_adder_2 (.in_1(dipswitch_6_p4), .in_2(dipswitch_5_p4), .S(half_adder_2_s[0]), .C(half_adder_2_c));
  Half_adder half_adder_3 (.in_1(half_adder_1_s), .in_2(in_14), .S(out_44), .C(half_adder_3_c));
  Full_Adder full_adder_1 (
    .Cin(half_adder_2_c), .A(dipswitch_6_p3), .B(dipswitch_5_p3), .Cout(full_adder_1_cout),
    .S(half_adder_2_s[1]));
  or or_28 (out_43, half_adder_1_c, half_adder_3_c);
  seven_segment_circuit16 seven_segment_circuit16_3 (
    .in_1(half_adder_2_s), .a(seven_segment_circuit16_3_a), .b(seven_segment_circuit16_3_b),
    .c(seven_segment_circuit16_3_c), .d(seven_segment_circuit16_3_d), .e(seven_segment_circuit16_3_e),
    .f(seven_segment_circuit16_3_f), .g(seven_segment_circuit16_3_g));
  Full_Adder full_adder_2 (
    .Cin(full_adder_1_cout), .A(dipswitch_6_p2), .B(dipswitch_5_p2), .Cout(full_adder_2_cout),
    .S(half_adder_2_s[2]));
  _7_Segment_Display u_7_segment_display_6 (
    .g(seven_segment_circuit16_3_g), .f(seven_segment_circuit16_3_f), .a(seven_segment_circuit16_3_a),
    .b(seven_segment_circuit16_3_b), .e(seven_segment_circuit16_3_e), .d(seven_segment_circuit16_3_d),
    .c(seven_segment_circuit16_3_c));  // open: dp
  LED led_2 (.in(full_adder_3_cout));
  Full_Adder full_adder_3 (
    .Cin(full_adder_2_cout), .A(dipswitch_6_p1), .B(dipswitch_5_p1), .Cout(full_adder_3_cout),
    .S(half_adder_2_s[3]));

  // Notes on the sheet:
  //   七段数码管译码器1
  //   2-4译码器实现3-8译码器
  //   16-4编码器
  //   1位2选1选择器
  //   3位4选1选择器
  //   七段数码管译码器2
  //   可切换进位计数制的七段数码管
  //   4位比较器
  //   通过半加器实现的全加器
endmodule

module decoder2_4 (
  input  in_1,
  input  in_2,
  output out_3,
  output out_4,
  output out_5,
  output out_6
);

  wire not_1_out, not_2_out;

  not not_1 (not_1_out, in_1);
  not not_2 (not_2_out, in_2);
  and and_1 (out_3, not_1_out, not_2_out);
  and and_2 (out_4, not_1_out, in_2);
  and and_3 (out_5, in_1, not_2_out);
  and and_4 (out_6, in_1, in_2);

  // Notes on the sheet:
  //   2-4译码器
endmodule

module seven_segment_circuit16 (
  input  [3:0] in_1,
  output a,
  output b,
  output c,
  output d,
  output e,
  output f,
  output g
);

  wire decoder_1_out0, decoder_1_out1, decoder_1_out2, decoder_1_out3, decoder_1_out4, decoder_1_out5,
       decoder_1_out6, decoder_1_out7, decoder_1_out8, decoder_1_out9, decoder_1_out10, decoder_1_out11,
       decoder_1_out12, decoder_1_out13, decoder_1_out14, decoder_1_out15;

  Decoder #(.enable("false"), .select(4)) decoder_1 (
    .out0(decoder_1_out0), .out1(decoder_1_out1), .out2(decoder_1_out2), .out3(decoder_1_out3),
    .out4(decoder_1_out4), .out5(decoder_1_out5), .out6(decoder_1_out6), .out7(decoder_1_out7),
    .out8(decoder_1_out8), .out9(decoder_1_out9), .out10(decoder_1_out10), .out11(decoder_1_out11),
    .out12(decoder_1_out12), .out13(decoder_1_out13), .out14(decoder_1_out14), .out15(decoder_1_out15),
    .sel(in_1));
  or or_1 (a, decoder_1_out10, decoder_1_out12, decoder_1_out0, decoder_1_out2, decoder_1_out3, decoder_1_out9, decoder_1_out5, decoder_1_out6, decoder_1_out7, decoder_1_out8, decoder_1_out14, decoder_1_out15);
  or or_2 (b, decoder_1_out10, decoder_1_out0, decoder_1_out1, decoder_1_out2, decoder_1_out3, decoder_1_out4, decoder_1_out8, decoder_1_out7, decoder_1_out9, decoder_1_out13);
  or or_3 (c, decoder_1_out5, decoder_1_out10, decoder_1_out0, decoder_1_out1, decoder_1_out3, decoder_1_out4, decoder_1_out6, decoder_1_out7, decoder_1_out8, decoder_1_out9, decoder_1_out11, decoder_1_out13);
  or or_4 (d, decoder_1_out11, decoder_1_out12, decoder_1_out0, decoder_1_out2, decoder_1_out3, decoder_1_out5, decoder_1_out6, decoder_1_out8, decoder_1_out9, decoder_1_out13, decoder_1_out14);
  or or_5 (e, decoder_1_out10, decoder_1_out11, decoder_1_out12, decoder_1_out0, decoder_1_out2, decoder_1_out6, decoder_1_out8, decoder_1_out13, decoder_1_out14, decoder_1_out15);
  or or_6 (f, decoder_1_out10, decoder_1_out11, decoder_1_out0, decoder_1_out4, decoder_1_out5, decoder_1_out12, decoder_1_out6, decoder_1_out8, decoder_1_out9, decoder_1_out14, decoder_1_out15);
  or or_7 (g, decoder_1_out5, decoder_1_out10, decoder_1_out11, decoder_1_out2, decoder_1_out3, decoder_1_out4, decoder_1_out6, decoder_1_out8, decoder_1_out9, decoder_1_out13, decoder_1_out14, decoder_1_out15);

  // Notes on the sheet:
  //   七段数码管译码器2
endmodule

module encoder16_4 (
  input  in_1,
  input  in_2,
  input  in_3,
  input  in_4,
  input  in_5,
  input  in_6,
  input  in_7,
  input  in_8,
  input  in_9,
  input  in_10,
  input  in_11,
  input  in_12,
  input  in_13,
  input  in_14,
  input  in_15,
  input  in_16,
  output out_17,
  output out_18,
  output out_19,
  output out_20
);

  or low1 (out_17, in_2, in_4, in_6, in_8, in_10, in_12, in_14, in_16);
  or or_1 (out_18, in_3, in_4, in_7, in_8, in_11, in_12, in_15, in_16);
  or or_2 (out_19, in_5, in_6, in_7, in_8, in_13, in_14, in_15, in_16);
  or high1 (out_20, in_9, in_10, in_11, in_12, in_13, in_14, in_15, in_16);
endmodule

module priority_encoder4_2 (
  input  \_4_2优先编码器 ,
  input  in_2,
  input  in_3,
  input  in_4,
  output out_5,
  output out_6
);

  wire and_1_out, and_2_out, not_1_out, not_2_out, not_3_out;

  not not_1 (not_1_out, in_3);
  not not_2 (not_2_out, in_4);
  not not_3 (not_3_out, in_4);
  and and_1 (and_1_out, in_2, not_1_out, not_2_out);
  and and_2 (and_2_out, in_3, not_3_out);
  or or_1 (out_5, in_4, and_1_out);
  or or_2 (out_6, and_2_out, in_4);
endmodule

module seven_segment_circuit10 (
  input  [3:0] in_1,
  output out_2,
  output out_3,
  output out_4,
  output out_5,
  output out_6,
  output out_7,
  output out_8,
  output out_9
);

  wire decoder_1_out0, decoder_1_out1, decoder_1_out2, decoder_1_out3, decoder_1_out4, decoder_1_out5,
       decoder_1_out6, decoder_1_out7, decoder_1_out8, decoder_1_out9, decoder_1_out10, decoder_1_out11,
       decoder_1_out12, decoder_1_out13, decoder_1_out14, decoder_1_out15;

  Decoder #(.enable("false"), .select(4)) decoder_1 (
    .out0(decoder_1_out0), .out1(decoder_1_out1), .out2(decoder_1_out2), .out3(decoder_1_out3),
    .out4(decoder_1_out4), .out5(decoder_1_out5), .out6(decoder_1_out6), .out7(decoder_1_out7),
    .out8(decoder_1_out8), .out9(decoder_1_out9), .out10(decoder_1_out10), .out11(decoder_1_out11),
    .out12(decoder_1_out12), .out13(decoder_1_out13), .out14(decoder_1_out14), .out15(decoder_1_out15),
    .sel(in_1));
  or or_1 (out_9, decoder_1_out15, decoder_1_out14, decoder_1_out13, decoder_1_out12, decoder_1_out11, decoder_1_out10);
  or or_2 (out_2, decoder_1_out0, decoder_1_out2, decoder_1_out3, decoder_1_out9, decoder_1_out5, decoder_1_out6, decoder_1_out7, decoder_1_out8);
  or or_3 (out_3, decoder_1_out0, decoder_1_out1, decoder_1_out2, decoder_1_out3, decoder_1_out4, decoder_1_out8, decoder_1_out7, decoder_1_out9);
  or or_4 (out_4, decoder_1_out0, decoder_1_out1, decoder_1_out3, decoder_1_out4, decoder_1_out5, decoder_1_out6, decoder_1_out7, decoder_1_out8, decoder_1_out9);
  or or_5 (out_5, decoder_1_out0, decoder_1_out2, decoder_1_out3, decoder_1_out5, decoder_1_out6, decoder_1_out8, decoder_1_out9);
  or or_6 (out_6, decoder_1_out0, decoder_1_out2, decoder_1_out6, decoder_1_out8);
  or or_7 (out_7, decoder_1_out0, decoder_1_out4, decoder_1_out5, decoder_1_out6, decoder_1_out8, decoder_1_out9);
  or or_8 (out_8, decoder_1_out2, decoder_1_out3, decoder_1_out4, decoder_1_out5, decoder_1_out6, decoder_1_out8, decoder_1_out9);

  // Notes on the sheet:
  //   七段数码管译码器1
endmodule

module Half_adder (
  input  in_1,
  input  in_2,
  output S,
  output C
);

  xor xor_1 (S, in_1, in_2);
  and and_1 (C, in_1, in_2);
endmodule

module Full_Adder (
  input  Cin,
  input  A,
  input  B,
  output Cout,
  output S
);

  wire and_1_out, and_2_out, or_1_out;

  and and_1 (and_1_out, A, B);
  and and_2 (and_2_out, Cin, or_1_out);
  or or_1 (or_1_out, B, A);
  xor xor_1 (S, Cin, A, B);
  or or_2 (Cout, and_2_out, and_1_out);
endmodule
