// Logisim project SequentialLogic.circ as structural Verilog: 3 circuits, main circuit main
module main (
  input  in_1,
  input  D,
  input  RE,
  input  RE_2,
  input  in_5,
  input  D_2,
  input  RE_3,
  output out_8,
  output out_9,
  output Q,
  output nQ,
  output Q_2,
  output nQ_2,
  output Q_3,
  output nQ_3,
  output nQ_4,
  output out_17,
  output out_18,
  output out_19,
  output out_20
);

  wire and_1_out, and_2_out, and_3_out, and_4_out, and_5_out, and_6_out, and_7_out, and_8_out, and_9_out,
       and_10_out, and_11_out, and_12_out, button_1_out, button_2_out, button_3_out, button_4_out,
       button_5_out, d_latch_1_q, d_latch_2_q, d_latch_3_q, d_latch_4_q, d_latch_5_q, d_latch_8_q,
       dipswitch_1_p1, dipswitch_2_p1, dipswitch_3_p1, dipswitch_4_p1, dipswitch_5_p1, dipswitch_6_p1,
       dipswitch_11_p1, dipswitch_12_p1, dipswitch_13_p1, dipswitch_14_p1, nor_1_out, nor_2_out, nor_3_out,
       not_1_out, not_2_out, not_3_out, not_4_out, not_5_out, not_6_out, not_7_out, not_8_out, not_9_out,
       not_10_out, not_11_out, not_12_out, not_13_out, not_15_out, or_1_out, or_2_out, sr_latch_3_q, undriven;

  // DipSwitch #(.number(1)) dipswitch_1: pin names not known; wires that end beside it: dipswitch_1_p1
  // DipSwitch #(.number(1)) dipswitch_2: pin names not known; wires that end beside it: dipswitch_2_p1
  // DipSwitch #(.number(1)) dipswitch_3: pin names not known; wires that end beside it: dipswitch_3_p1
  // DipSwitch #(.number(1)) dipswitch_4: pin names not known; wires that end beside it: dipswitch_4_p1
  not not_1 (not_1_out, dipswitch_1_p1);
  // DipSwitch #(.number(1)) dipswitch_5: pin names not known; wires that end beside it: dipswitch_5_p1
  // DipSwitch #(.number(1)) dipswitch_6: pin names not known; wires that end beside it: dipswitch_6_p1
  // DipSwitch #(.number(1)) dipswitch_7: pin names not known
  buf and_1 (and_1_out, dipswitch_2_p1);  // AND_Gate
  buf and_2 (and_2_out, dipswitch_2_p1);  // AND_Gate
  // DipSwitch #(.number(1)) dipswitch_8: pin names not known
  // DipSwitch #(.number(1)) dipswitch_9: pin names not known
  buf and_3 (and_3_out, dipswitch_3_p1);  // AND_Gate
  buf and_4 (and_4_out, dipswitch_3_p1);  // AND_Gate
  // DipSwitch #(.number(1)) dipswitch_10: pin names not known
  not not_2 (not_2_out, dipswitch_11_p1);
  // DipSwitch #(.number(1)) dipswitch_11: pin names not known; wires that end beside it: dipswitch_11_p1
  not not_3 (not_3_out, dipswitch_12_p1);
  // DipSwitch #(.number(1)) dipswitch_12: pin names not known; wires that end beside it: dipswitch_12_p1
  not not_4 (not_4_out, button_1_out);
  Button button_1 (.out(button_1_out));
  Button button_2 (.out(button_2_out));
  not not_5 (not_5_out, D);
  Button button_3 (.out(button_3_out));
  not not_6 (not_6_out, not_15_out);
  Button button_4 (.out(button_4_out));
  Button button_5 (.out(button_5_out));
  not not_7 (not_7_out, D_2);
  and and_5 (and_5_out, dipswitch_1_p1, dipswitch_4_p1);
  and and_6 (and_6_out, dipswitch_4_p1, not_1_out);
  and and_7 (and_7_out, dipswitch_5_p1, not_2_out);
  // DipSwitch #(.number(1)) dipswitch_13: pin names not known; wires that end beside it: dipswitch_13_p1
  or or_1 (or_1_out, dipswitch_11_p1, not_8_out);
  not not_8 (not_8_out, dipswitch_5_p1);
  and and_8 (and_8_out, undriven, not_3_out);
  // DipSwitch #(.number(1)) dipswitch_14: pin names not known; wires that end beside it: dipswitch_14_p1
  or or_2 (or_2_out, dipswitch_12_p1, not_9_out);
  not not_9 (not_9_out, undriven);
  not not_10 (not_10_out, button_2_out);
  nor nor_1 (nor_1_out, not_5_out, RE);
  not not_11 (not_11_out, button_3_out);
  nor nor_2 (nor_2_out, not_6_out, RE_2);
  not not_12 (not_12_out, button_4_out);
  not not_13 (not_13_out, button_5_out);
  nor nor_3 (nor_3_out, not_7_out, RE_3);
  nor nor_4 (out_8, and_1_out, out_9);
  nor nor_5 (out_9, out_8, and_2_out);
  nand nand_1 (Q, and_3_out, nQ);
  nand nand_2 (nQ, Q, and_4_out);
  and and_9 (and_9_out, and_7_out, dipswitch_13_p1);
  and and_10 (and_10_out, dipswitch_13_p1, or_1_out);
  and and_11 (and_11_out, and_8_out, dipswitch_14_p1);
  and and_12 (and_12_out, dipswitch_14_p1, or_2_out);
  SR_Latch sr_latch_1 (.R(and_6_out), .S(and_5_out), .Q(Q_2), .NQ(nQ_2));
  D_Latch d_latch_1 (.WE(not_4_out), .D(in_1), .Q(d_latch_1_q));  // open: NQ
  D_Latch d_latch_2 (.WE(not_10_out), .D(nor_1_out), .Q(d_latch_2_q));  // open: NQ
  D_Latch d_latch_3 (.WE(not_11_out), .D(nor_2_out), .Q(d_latch_3_q));  // open: NQ
  D_Latch d_latch_4 (.WE(button_4_out), .D(in_5), .Q(d_latch_4_q));  // open: NQ
  D_Latch d_latch_5 (.WE(not_13_out), .D(nor_3_out), .Q(d_latch_5_q));  // open: NQ
  SR_Latch sr_latch_2 (.R(and_10_out), .S(and_9_out), .Q(Q_3), .NQ(nQ_3));
  not not_14 (dipswitch_6_p1, sr_latch_3_q);
  SR_Latch sr_latch_3 (.R(and_12_out), .S(and_11_out), .Q(sr_latch_3_q), .NQ(nQ_4));
  D_Latch d_latch_6 (.WE(button_1_out), .D(d_latch_1_q), .Q(out_17));  // open: NQ
  D_Latch d_latch_7 (.WE(button_2_out), .D(d_latch_2_q), .Q(out_18));  // open: NQ
  not not_15 (not_15_out, d_latch_8_q);
  D_Latch d_latch_8 (.WE(button_3_out), .D(d_latch_3_q), .Q(d_latch_8_q));  // open: NQ
  D_Latch d_latch_9 (.WE(not_12_out), .D(d_latch_4_q), .Q(out_19));  // open: NQ
  D_Latch d_latch_10 (.WE(button_5_out), .D(d_latch_5_q), .Q(out_20));  // open: NQ

  // Notes on the sheet:
  //   D锁存器
  //   D
  //   D触发器
  //   SR锁存器
  //   ~S~R锁存器
  //   R
  //   S
  //   WE
  //   带复位的D锁存器
  //   R
  //   D
  //   D锁存器实现位翻转功能
  //   R
  //   D
  //   带复位的D触发器
  //   D触发器实现位翻转
  //   下降沿D触发器
  //   带使能的D触发器
  //   WE
  //   WE
  //   Q
endmodule

module SR_Latch (
  input  R,
  input  S,
  output Q,
  output NQ
);

  nor nor_1 (Q, R, NQ);
  nor nor_2 (NQ, Q, S);

  // Notes on the sheet:
  //   SR锁存器
endmodule

module D_Latch (
  input  WE,
  input  D,
  output Q,
  output NQ
);

  wire and_1_out, and_2_out, not_1_out;

  not not_1 (not_1_out, D);
  and and_1 (and_1_out, D, WE);
  and and_2 (and_2_out, WE, not_1_out);
  SR_Latch sr_latch_1 (.R(and_2_out), .S(and_1_out), .Q(Q), .NQ(NQ));

  // Notes on the sheet:
  //   D
  //   D锁存器
  //   WE
  //   Q
  //   ~Q
endmodule
