// Logisim project minirv.circ as structural Verilog: 5 circuits, main circuit main
module main (
  input  in_1
);

  wire addiop, clk, comparator_1_eq, comparator_2_eq, comparator_3_eq, comparator_4_eq, jalrop, wen;
  wire [2:0] priority_encoder_1_out;
  wire [4:0] addi_rd, addi_rs1, and_5_out, and_6_out, and_7_out, and_8_out, bit_extender_3_out,
       bit_extender_4_out, bit_extender_5_out, bit_extender_6_out, jalr_rd, jalr_rs1, raddr1, raddr2, waddr;
  wire [31:0] adder_1_out, addi_rddata, addi_rs1data, and_3_out, and_4_out, bit_extender_1_out,
       bit_extender_2_out, jalr_newpc, jalr_rddata, jalr_rs1data, multiplexer_1_out, PC, rdata1, rdata2,
       rom_t1_1_out_2, wdata;

  Button button_1 (.out(clk));
  Register #(.width(32)) u_PC (.D(multiplexer_1_out), .en(in_1), .clk(clk), .Q(PC));  // open: clr
  Adder #(.width(32)) adder_1 (.a(32'h4), .b(PC), .out(adder_1_out));  // open: cin, cout
  Multiplexer #(.width(32)) multiplexer_1 (.in0(adder_1_out), .in1(jalr_newpc), .out(multiplexer_1_out), .sel(jalrop));
  ROM_t1 rom_t1_1 (.in_1(PC), .out_2(rom_t1_1_out_2));
  Comparator #(.width(3)) comparator_1 (.a(rom_t1_1_out_2[14:12]), .b(3'b000), .eq(comparator_1_eq));  // open: gt, lt
  Comparator #(.width(7)) comparator_2 (.a(rom_t1_1_out_2[6:0]), .b(7'b1100111), .eq(comparator_2_eq));  // open: gt, lt
  Comparator #(.width(7)) comparator_3 (.a(rom_t1_1_out_2[6:0]), .b(7'b0010011), .eq(comparator_3_eq));  // open: gt, lt
  Comparator #(.width(3)) comparator_4 (.a(3'b000), .b(rom_t1_1_out_2[14:12]), .eq(comparator_4_eq));  // open: gt, lt
  and and_1 (jalrop, comparator_1_eq, comparator_2_eq);
  and and_2 (addiop, comparator_3_eq, comparator_4_eq);
  or or_1 (wen, jalrop, addiop);
  assign bit_extender_1_out = {{31{jalrop}}, jalrop};  // Bit_Extender bit_extender_1
  assign bit_extender_2_out = {{31{addiop}}, addiop};  // Bit_Extender bit_extender_2
  assign bit_extender_3_out = {{4{jalrop}}, jalrop};  // Bit_Extender bit_extender_3
  assign bit_extender_4_out = {{4{addiop}}, addiop};  // Bit_Extender bit_extender_4
  assign and_3_out = bit_extender_1_out & jalr_rddata;  // AND_Gate and_3, 32 bits wide
  assign and_4_out = addi_rddata & bit_extender_2_out;  // AND_Gate and_4, 32 bits wide
  assign and_5_out = bit_extender_3_out & jalr_rd;  // AND_Gate and_5, 5 bits wide
  assign and_6_out = addi_rd & bit_extender_4_out;  // AND_Gate and_6, 5 bits wide
  assign wdata = and_3_out | and_4_out;  // OR_Gate or_2, 32 bits wide
  my_jalr my_jalr_1 (
    .I(rom_t1_1_out_2), .rs1data(jalr_rs1data), .PC(PC), .rd(jalr_rd), .rs1(jalr_rs1), .newpc(jalr_newpc),
    .rddata(jalr_rddata));
  my_addi my_addi_1 (.I(rom_t1_1_out_2), .rs1data(addi_rs1data), .rd(addi_rd), .rs1(addi_rs1), .rddata(addi_rddata));
  assign waddr = and_5_out | and_6_out;  // OR_Gate or_3, 5 bits wide
  assign bit_extender_5_out = {{4{jalrop}}, jalrop};  // Bit_Extender bit_extender_5
  assign bit_extender_6_out = {{4{addiop}}, addiop};  // Bit_Extender bit_extender_6
  Demultiplexer #(.select(3), .width(32)) demultiplexer_1 (
    .out0(addi_rs1data), .out1(jalr_rs1data), .in(rdata1), .sel(priority_encoder_1_out));  // open: out2, out3, out4, out5, out6, out7
  Priority_Encoder priority_encoder_1 (
    .in0(addiop), .in1(jalrop), .in2(1'b0), .in3(1'b0), .in4(1'b0), .in5(1'b0), .in6(1'b0), .in7(1'b0),
    .out(priority_encoder_1_out));  // open: en_in, gs, en_out
  assign and_7_out = bit_extender_5_out & jalr_rs1;  // AND_Gate and_7, 5 bits wide
  assign and_8_out = addi_rs1 & bit_extender_6_out;  // AND_Gate and_8, 5 bits wide
  assign raddr1 = and_7_out | and_8_out;  // OR_Gate or_4, 5 bits wide
  GPR gpr_1 (
    .clk(clk), .wdata(wdata), .waddr(waddr), .wen(wen), .raddr1(raddr1), .raddr2(raddr2), .rdata1(rdata1),
    .rdata2(rdata2));

  // Notes on the sheet:
  //   jalr
  //   addi
  //   写端口
  //   读1
endmodule

module GPR (
  input  clk,
  input  [31:0] wdata,
  input  [4:0] waddr,
  input  wen,
  input  [4:0] raddr1,
  input  [4:0] raddr2,
  output [31:0] rdata1,
  output [31:0] rdata2
);

  wire decoder_1_out1, decoder_1_out2, decoder_1_out3, decoder_1_out4, decoder_1_out5, decoder_1_out6,
       decoder_1_out7, decoder_1_out8, decoder_1_out9, decoder_1_out10, decoder_1_out11, decoder_1_out12,
       decoder_1_out13, decoder_1_out14, decoder_1_out15;
  wire [31:0] register_1_q, register_2_q, register_3_q, register_4_q, register_5_q, register_6_q,
       register_7_q, register_8_q, register_9_q, register_10_q, register_11_q, register_12_q, register_13_q,
       register_14_q, register_15_q, register_16_q;

  Decoder #(.select(4)) decoder_1 (
    .out1(decoder_1_out1), .out2(decoder_1_out2), .out3(decoder_1_out3), .out4(decoder_1_out4),
    .out5(decoder_1_out5), .out6(decoder_1_out6), .out7(decoder_1_out7), .out8(decoder_1_out8),
    .out9(decoder_1_out9), .out10(decoder_1_out10), .out11(decoder_1_out11), .out12(decoder_1_out12),
    .out13(decoder_1_out13), .out14(decoder_1_out14), .out15(decoder_1_out15), .sel(waddr[3:0]), .en(wen));  // open: out0
  Register #(.width(32)) register_1 (.D(wdata), .en(decoder_1_out1), .clk(clk), .Q(register_1_q), .clr(1'b1));
  Register #(.width(32)) register_2 (.D(wdata), .en(decoder_1_out8), .clk(clk), .Q(register_2_q));  // open: clr
  Register #(.width(32)) register_3 (.D(wdata), .en(decoder_1_out1), .clk(clk), .Q(register_3_q));  // open: clr
  Register #(.width(32)) register_4 (.D(wdata), .en(decoder_1_out9), .clk(clk), .Q(register_4_q));  // open: clr
  Register #(.width(32)) register_5 (.D(wdata), .en(decoder_1_out2), .clk(clk), .Q(register_5_q));  // open: clr
  Register #(.width(32)) register_6 (.D(wdata), .en(decoder_1_out10), .clk(clk), .Q(register_6_q));  // open: clr
  Register #(.width(32)) register_7 (.D(wdata), .en(decoder_1_out3), .clk(clk), .Q(register_7_q));  // open: clr
  Register #(.width(32)) register_8 (.D(wdata), .en(decoder_1_out11), .clk(clk), .Q(register_8_q));  // open: clr
  Register #(.width(32)) register_9 (.D(wdata), .en(decoder_1_out4), .clk(clk), .Q(register_9_q));  // open: clr
  Register #(.width(32)) register_10 (.D(wdata), .en(decoder_1_out12), .clk(clk), .Q(register_10_q));  // open: clr
  Register #(.width(32)) register_11 (.D(wdata), .en(decoder_1_out5), .clk(clk), .Q(register_11_q));  // open: clr
  Register #(.width(32)) register_12 (.D(wdata), .en(decoder_1_out13), .clk(clk), .Q(register_12_q));  // open: clr
  Register #(.width(32)) register_13 (.D(wdata), .en(decoder_1_out6), .clk(clk), .Q(register_13_q));  // open: clr
  Register #(.width(32)) register_14 (.D(wdata), .en(decoder_1_out14), .clk(clk), .Q(register_14_q));  // open: clr
  Register #(.width(32)) register_15 (.D(wdata), .en(decoder_1_out7), .clk(clk), .Q(register_15_q));  // open: clr
  Register #(.width(32)) register_16 (.D(wdata), .en(decoder_1_out15), .clk(clk), .Q(register_16_q));  // open: clr
  Multiplexer #(.select(4), .width(32)) multiplexer_1 (
    .in0(register_1_q), .in1(register_3_q), .in2(register_5_q), .in3(register_7_q), .in4(register_9_q),
    .in5(register_11_q), .in6(register_13_q), .in7(register_15_q), .in8(register_2_q), .in9(register_4_q),
    .in10(register_6_q), .in11(register_8_q), .in12(register_10_q), .in13(register_12_q),
    .in14(register_14_q), .in15(register_16_q), .out(rdata1), .sel(raddr1[3:0]));
  Multiplexer #(.select(4), .width(32)) multiplexer_2 (
    .in0(register_1_q), .in1(register_3_q), .in2(register_5_q), .in3(register_7_q), .in4(register_9_q),
    .in5(register_11_q), .in6(register_13_q), .in7(register_15_q), .in8(register_2_q), .in9(register_4_q),
    .in10(register_6_q), .in11(register_8_q), .in12(register_10_q), .in13(register_12_q),
    .in14(register_14_q), .in15(register_16_q), .out(rdata2), .sel(raddr2[3:0]));
endmodule

module ROM_t1 (
  input  [31:0] in_1,
  output [31:0] out_2
);

  ROM #(.dataWidth(32)) rom_1 (.addr(in_1[9:2]), .data(out_2));

  // Notes on the sheet:
  //   contents of rom_1 (hex, n*v repeats v):
  //   1400513 10000e7 c000e7 c00067 a50513 8067
endmodule

module my_addi (
  input  [31:0] I,
  input  [31:0] rs1data,
  output [4:0] rd,
  output [4:0] rs1,
  output [31:0] rddata
);

  wire [31:0] bit_extender_1_out;

  assign bit_extender_1_out = {{20{I[31]}}, I[31:20]};  // Bit_Extender bit_extender_1
  Adder #(.width(32)) adder_1 (.a(bit_extender_1_out), .b(rs1data), .out(rddata));  // open: cin, cout

  assign rd = I[11:7];
  assign rs1 = I[19:15];
endmodule

module my_jalr (
  input  [31:0] I,
  input  [31:0] rs1data,
  input  [31:0] PC,
  output [4:0] rd,
  output [4:0] rs1,
  output [31:0] newpc,
  output [31:0] rddata
);

  wire [31:0] bit_extender_1_out;

  assign bit_extender_1_out = {{20{I[31]}}, I[31:20]};  // Bit_Extender bit_extender_1
  Adder #(.width(32)) adder_1 (.a(PC), .b(32'h4), .out(rddata));  // open: cin, cout
  Adder #(.width(32)) adder_2 (.a(bit_extender_1_out), .b(rs1data), .out(newpc));  // open: cin, cout

  assign rd = I[11:7];
  assign rs1 = I[19:15];

  // Notes on the sheet:
  //   把当前的下一条指令地址存入rd
endmodule
